# Fritzing sketch Sketch (saved by Fritzing 0.9.2b)
breadboards: 1

parts:
  RPI_B+ = Raspberry Pi B+
  HMC5883L = Triple Axis Magnetometer - HMC5883 Breakout
  M1 = DC Motor
  M2 = DC Motor
  L298N1 = L298_BRIDGE_DRIVER [package=powerso20]
  VCC = 4 x AAA Battery Mount

nets:
  3V3: RPI_B+.3v3, HMC5883L.VCC
  N1: RPI_B+.GPIO2, HMC5883L.SDA
  N2: RPI_B+.GPIO3, HMC5883L.SCL
  N3: RPI_B+.GPIO19, L298N1.IN1
  N4: RPI_B+.GPIO26, L298N1.IN2
  GND: RPI_B+.GND, HMC5883L.GND
  N5: RPI_B+.GPIO20, L298N1.IN4
  N6: RPI_B+.GPIO16, L298N1.IN3
  5V: RPI_B+.5V, L298N1.VSS
  N7: M1.pin_1, L298N1.OUT3
  N8: M1.pin_2, L298N1.OUT4
  N9: M2.pin_1, L298N1.OUT1
  N10: M2.pin_2, L298N1.OUT2
  N11: L298N1.GND, VCC.-
  N12: L298N1.VS, VCC.+
